# Fritzing sketch humidity circuit (saved by Fritzing 0.9.3b)
breadboards: 1

parts:
  Part2 = Arduino Uno (Rev3)
  U1 = RELAY [package=relay-jzc]
  J1 = Basic Servo
  Part9 = Soil Moisture Sensor
  Part10 = Soil Moisture Sensor
  S1 = Pushbutton [package="[THT]"]
  LED3 = LED - 5mm [color="Green (555nm)" package="5 mm [THT]"]
  R1 = Resistor [tolerance=±5% resistance=220 package="0805 [SMD]"]
  R2 = Resistor [tolerance=±5% resistance=220 package="0805 [SMD]"]
  M1 = DC Motor  # not connected
  Power_plug1 = Power plug

nets:
  N1: Part2.A3, Part9.SIG
  N2: Part2.A4/SDA, Part10.SIG
  N3: Part2.D11_PWM/MOSI, LED3.anode
  N4: Part2.D12/MISO, U1.COIL2
  N5: Part2.D13/SCK, J1.pulse
  N6: Part2.D7, S1.Pin_1, S1.Pin_2, R2.Pin_0
  VCC: Part2.3V3, Part9.VCC, Part10.VCC
  5V: Part2.5V, U1.NO, J1.vcc, S1.Pin_3, S1.Pin_4
  GND: Part2.GND, U1.NC, J1.gnd, Part9.GND, Part10.GND, R1.Pin_0, R2.Pin_1
  N7: U1.MAIN, Power_plug1.VCC
  N8: LED3.cathode, R1.Pin_1
