# Fritzing sketch servo circuit (saved by Fritzing 0.9.3b)
breadboards: 1

parts:
  part = Arduino Uno (Rev3)
  J1 = Basic Servo

nets:
  N1: part.D13/SCK, J1.gnd
  N2: part.GND, J1.pulse
  5V: part.5V, J1.vcc
